# Fritzing sketch Project_Veroboard_Sketch (saved by Fritzing 0.9.3b)
stripboards: 1

parts:
  IC1 = IC, DIP package, 28 pins [chip_label=IC]

nets:
  N1: IC1.pin1, IC1.pin28
  N2: IC1.pin2, IC1.pin27
  N3: IC1.pin3, IC1.pin26
  N4: IC1.pin4, IC1.pin25
  N5: IC1.pin5, IC1.pin24
  N6: IC1.pin6, IC1.pin23
  N7: IC1.pin7, IC1.pin22
  N8: IC1.pin8, IC1.pin21
  N9: IC1.pin9, IC1.pin20
  N10: IC1.pin10, IC1.pin19
  N11: IC1.pin11, IC1.pin18
  N12: IC1.pin12, IC1.pin17
  N13: IC1.pin13, IC1.pin16
  N14: IC1.pin14, IC1.pin15
